# Fritzing sketch Project 1 Fritzing (saved by Fritzing 0.9.3b)
breadboards: 2

parts:
  Part1 = Arduino Uno (Rev3)  # not connected
  Part2 = 2A MOTOR SHIELD 9
  hc-sr1 = hc-sr04
  T1 = LM35 Temperature Sensor [package="TO92 [THT]"]
  J1 = Basic Servo
  M2 = DC Motor  # not connected
  M3 = DC Motor  # not connected
  3-pins_Hall_Effect_Sensor1 = mystery part, 3 pins [chip_label="Hall Effect Sensor"]
  3-pins_Hall_Effect_Sensor2 = mystery part, 3 pins [chip_label="Hall Effect Sensor"]
  LCD1 = LCD screen
  R1 = Resistor [tolerance=±5% resistance=10k package="2512 [SMD]"]
  U1 = POT [package=pot_alpha_rv16af-20]
  Q1 = PHOTOTRANSISTOR REFLECTIVE OBJECT SENSOR [package=qrb1114-side]
  Q2 = PHOTOTRANSISTOR REFLECTIVE OBJECT SENSOR [package=qrb1114-side]
  R3 = Resistor [tolerance=±5% resistance=220 package="2512 [SMD]"]
  R4 = Resistor [tolerance=±5% resistance=220 package="2512 [SMD]"]
  R5 = Resistor [tolerance=±5% resistance=220 package="2512 [SMD]"]
  R6 = Resistor [tolerance=±5% resistance=220 package="2512 [SMD]"]

nets:
  N1: Part2.D3, 3-pins_Hall_Effect_Sensor1.pin1
  N2: Part2.D11, LCD1.RS
  N3: Part2.A4, LCD1.DB6
  N4: Part2.A1, J1.pulse
  N5: Part2.D13, hc-sr1.Trig
  N6: Part2.A2, Q1.C, R3.Pin_1
  N7: Part2.D2, 3-pins_Hall_Effect_Sensor2.pin1
  N8: Part2.D10, LCD1.E
  N9: Part2.A5, LCD1.DB7
  N10: Part2.A0, T1.+Vs
  N11: Part2.D12, hc-sr1.Echo
  N12: Part2.A3, Q2.C, R5.Pin_1
  N13: Part2.D8, LCD1.DB5
  N14: Part2.D9, LCD1.DB4
  VCC: hc-sr1.VCC, T1.Vout, J1.vcc, 3-pins_Hall_Effect_Sensor1.pin3, 3-pins_Hall_Effect_Sensor2.pin3, R1.Pin_0, U1.S, Q1.A, Q2.A, R3.Pin_0, R5.Pin_0
  GND: hc-sr1.GND, T1.GND, J1.gnd, 3-pins_Hall_Effect_Sensor1.pin2, 3-pins_Hall_Effect_Sensor2.pin2, LCD1.VSS, LCD1.R/W, LCD1.LED-, U1.E, Q1.E, Q2.E, R4.Pin_0, R6.Pin_0
  N15: LCD1.LED+, R1.Pin_1
  N16: Q1.K, R4.Pin_1
  N17: Q2.K, R6.Pin_1
